// Logisim project cpu.circ as structural Verilog: 12 circuits, main circuit main
module main (
  input  Rst
);

  wire and_1_out, Clk_out, jsd_1_weo, not_1_out, sr_1_fo, sr_1_ho, undriven, undriven_8, undriven_10;
  wire [1:0] undriven_2;
  wire [4:0] undriven_9;
  wire [6:0] undriven_4;
  wire [7:0] ar_1_adho, ar_1_adlo, ir_1_do, memory_1_do, pc_1_adho, pc_1_adlo, undriven_5;
  wire [8:0] undriven_3;
  wire [11:0] undriven_6;
  wire [12:12] undriven_7;

  JSD jsd_1 (.WEI(undriven_3[1]), .JE(sr_1_fo), .IJE(undriven), .WEO(jsd_1_weo));
  AR ar_1 (
    .ADLI(pc_1_adlo), .ADHI(pc_1_adho), .Clk(and_1_out), .Rst(Rst), .ADLO(ar_1_adlo), .ADHO(ar_1_adho));  // open: LWE, HWE
  PC pc_1 (
    .Reset(Rst), .WE(jsd_1_weo), .CE(undriven_3[0]), .Clk(and_1_out), .ADLI(pc_1_adlo), .ADHI(pc_1_adho),
    .OE(undriven_3[2]), .ADLO(pc_1_adlo), .ADHO(pc_1_adho));
  Memory memory_1 (
    .WE(undriven_2[0]), .Clk(and_1_out), .DI(memory_1_do), .ADL(ar_1_adlo), .ADH(ar_1_adho),
    .OE(undriven_2[1]), .DO(memory_1_do));
  SP sp_1 (.WE(undriven_3[7]), .DI(memory_1_do), .Clk(and_1_out), .Reset(Rst), .OE(undriven_3[8]), .DO(memory_1_do));
  IR ir_1 (.WE(undriven_4[0]), .DI(memory_1_do), .Clk(and_1_out), .Reset(Rst), .DO(ir_1_do));
  Registers registers_1 (
    .AWE(undriven_4[1]), .XWE(undriven_4[3]), .YWE(undriven_4[5]), .DBI(memory_1_do), .Clk(and_1_out),
    .Reset(Rst), .AO(undriven_5), .AOE(undriven_4[2]), .XOE(undriven_4[4]), .YOE(undriven_4[6]),
    .DBO(memory_1_do));
  ALU alu_1 (
    .BOr(undriven_6[5]), .BXOr(undriven_6[6]), .Shl(undriven_6[7]), .Shr(undriven_6[8]),
    .BNot(undriven_6[9]), .Inc(undriven_6[10]), .Dec(undriven_6[11]), .OE(undriven_7[12]), .Rst(Rst),
    .Clk(and_1_out), .DBI(memory_1_do), .AI(undriven_5), .Add(undriven_6[0]), .Sub(undriven_6[1]),
    .Mul(undriven_6[2]), .Div(undriven_6[3]), .BAnd(undriven_6[4]), .DBO(memory_1_do));  // open: C, Z
  Const const_1 (.OE1(undriven_8), .D(memory_1_do));
  CSD csd_1 ();  // open: Opcode, AIO, AXO, ASL, ASR, ANO, AIN, ADE, ALO, PCE, PCI, PCO, LAI, LAO, HAI, HAO, SPI, SPO, MEI, MEO, IRI, ARI, ARO, XRI, XRO, YRI, YRO, SRI, SRO, RFI, CFI, IFS, IFC, HFS, ZFO, CFO, EFO, LFO, GFO, IFO, AAD, ASU, AMU, ADI, AAN
  SR sr_1 (
    .WE(undriven_10), .DI(memory_1_do), .Clk(and_1_out), .Rst(Rst), .ZE(undriven_9[0]), .CE(undriven_9[1]),
    .EE(undriven_9[2]), .LE(undriven_9[3]), .GE(undriven_9[4]), .DO(memory_1_do), .FO(sr_1_fo), .HO(sr_1_ho));  // open: IO
  and and_1 (and_1_out, not_1_out, Clk_out);
  not not_1 (not_1_out, sr_1_ho);
  Clock Clk (.out(Clk_out));

  // Notes on the sheet:
  //   Opcode
  //   CONTROL SIGNAL DECODER
endmodule

module Memory (
  input  WE,
  input  Clk,
  input  [7:0] DI,
  input  OE,
  input  [7:0] ADL,
  input  [7:0] ADH,
  output [7:0] DO
);

  wire and_1_out, not_1_out, not_2_out;
  wire [7:0] controlled_buffer_1_out, ram_1_dout, rom_1_data;

  not not_1 (not_1_out, ADH[7]);
  RAM #(.addrWidth(15)) ram_1 (
    .addr({ADH[6:0], ADL}), .we(and_1_out), .oe(1'b1), .clk(Clk), .din(DI), .dout(ram_1_dout));
  and and_1 (and_1_out, WE, not_1_out);
  ROM #(.addrWidth(15)) rom_1 (.addr({ADH[6:0], ADL}), .data(rom_1_data));
  assign controlled_buffer_1_out = not_2_out ? ram_1_dout : 8'bz;  // Controlled_Buffer controlled_buffer_1
  not not_2 (not_2_out, ADH[7]);
  assign DO = OE ? controlled_buffer_1_out : 8'bz;  // Controlled_Buffer controlled_buffer_2
  assign controlled_buffer_1_out = ADH[7] ? rom_1_data : 8'bz;  // Controlled_Buffer controlled_buffer_3
endmodule

module PC (
  input  Reset,
  input  WE,
  input  CE,
  input  Clk,
  input  OE,
  input  [7:0] ADLI,
  input  [7:0] ADHI,
  output [7:0] ADLO,
  output [7:0] ADHO
);

  wire [15:0] counter_1_q;

  Counter #(.max('hffff), .width(16)) counter_1 (
    .clr(Reset), .load(WE), .up(1'b1), .count(CE), .clk(Clk), .D({ADHI, ADLI}), .Q(counter_1_q));  // open: carry
  assign {ADHO, ADLO} = OE ? counter_1_q : 16'bz;  // Controlled_Buffer controlled_buffer_1
endmodule

module Registers (
  input  Clk,
  input  Reset,
  input  [7:0] DBI,
  input  [7:0] AO,
  input  AOE,
  input  AWE,
  input  XOE,
  input  XWE,
  input  YOE,
  input  YWE,
  output [7:0] DBO
);

  wire [7:0] register_2_q, register_3_q;

  Register register_1 (.D(DBI), .en(AWE), .clk(Clk), .Q(AO), .clr(Reset));
  Register register_2 (.D(DBI), .en(XWE), .clk(Clk), .Q(register_2_q), .clr(Reset));
  Register register_3 (.D(DBI), .en(YWE), .clk(Clk), .Q(register_3_q), .clr(Reset));
  assign DBO = AOE ? AO : 8'bz;  // Controlled_Buffer controlled_buffer_1
  assign DBO = XOE ? register_2_q : 8'bz;  // Controlled_Buffer controlled_buffer_2
  assign DBO = YOE ? register_3_q : 8'bz;  // Controlled_Buffer controlled_buffer_3
endmodule

module CSD (
  input  [7:0] Opcode,
  output PCE,
  output PCI,
  output PCO,
  output LAI,
  output LAO,
  output HAI,
  output HAO,
  output SPI,
  output SPO,
  output MEI,
  output MEO,
  output IRI,
  output ARI,
  output ARO,
  output XRI,
  output XRO,
  output YRI,
  output YRO,
  output SRI,
  output SRO,
  output RFI,
  output CFI,
  output IFS,
  output IFC,
  output HFS,
  output ZFO,
  output CFO,
  output EFO,
  output LFO,
  output GFO,
  output IFO,
  output AAD,
  output ASU,
  output AMU,
  output ADI,
  output AAN,
  output AIO,
  output AXO,
  output ASL,
  output ASR,
  output ANO,
  output AIN,
  output ADE,
  output ALO
);

  wire [47:44] rom_1_data;

  ROM #(.dataWidth(48)) rom_1 (
    .addr(Opcode),
    .data({rom_1_data, ALO, ADE, AIN, ANO, ASR, ASL, AXO, AIO, AAN, ADI, AMU, ASU, AAD, IFO, GFO, LFO, EFO, CFO, ZFO, HFS, IFC, IFS, CFI, RFI, SRO, SRI, YRO, YRI, XRO, XRI, ARO, ARI, IRI, MEO, MEI, SPO, SPI, HAO, HAI, LAO, LAI, PCO, PCI, PCE}));
endmodule

module ALU (
  input  Add,
  input  Sub,
  input  Mul,
  input  Div,
  input  BAnd,
  input  BOr,
  input  BXOr,
  input  Shl,
  input  Shr,
  input  BNot,
  input  Inc,
  input  Dec,
  input  [7:0] DBI,
  input  OE,
  input  [7:0] AI,
  input  Rst,
  input  Clk,
  output [7:0] DBO,
  output C,
  output Z
);

  wire adder_1_cout, subtractor_1_bout;
  wire [7:0] adder_1_out, adder_2_out, and_2_out, controlled_buffer_1_out, divider_1_out, multiplier_1_cout,
       multiplier_1_out, not_1_out, or_1_out, register_1_q, shifter_1_out, shifter_2_out, subtractor_1_out,
       subtractor_2_out, xor_1_out;

  assign controlled_buffer_1_out = Add ? adder_1_out : 8'bz;  // Controlled_Buffer controlled_buffer_1
  Adder adder_1 (.a(AI), .b(DBI), .out(adder_1_out), .cout(adder_1_cout));  // open: cin
  assign C = Add ? adder_1_cout : 1'bz;  // Controlled_Buffer controlled_buffer_2
  assign controlled_buffer_1_out = Sub ? subtractor_1_out : 8'bz;  // Controlled_Buffer controlled_buffer_3
  Subtractor subtractor_1 (.a(AI), .b(DBI), .out(subtractor_1_out), .bout(subtractor_1_bout));  // open: bin
  assign C = Sub ? subtractor_1_bout : 1'bz;  // Controlled_Buffer controlled_buffer_4
  assign controlled_buffer_1_out = Mul ? multiplier_1_out : 8'bz;  // Controlled_Buffer controlled_buffer_5
  Multiplier multiplier_1 (.b(DBI), .out(multiplier_1_out), .cout(multiplier_1_cout));  // open: a, cin
  assign controlled_buffer_1_out = Div ? divider_1_out : 8'bz;  // Controlled_Buffer controlled_buffer_6
  Divider divider_1 (.a(AI), .b(DBI), .out(divider_1_out));  // open: upper, rem
  and and_1 (C, multiplier_1_cout[0], multiplier_1_cout[1], multiplier_1_cout[2], multiplier_1_cout[3], multiplier_1_cout[4], multiplier_1_cout[5], multiplier_1_cout[6], multiplier_1_cout[7]);
  assign and_2_out = AI & DBI;  // AND_Gate and_2, 8 bits wide
  assign controlled_buffer_1_out = BAnd ? and_2_out : 8'bz;  // Controlled_Buffer controlled_buffer_7
  assign or_1_out = AI | DBI;  // OR_Gate or_1, 8 bits wide
  assign controlled_buffer_1_out = BOr ? or_1_out : 8'bz;  // Controlled_Buffer controlled_buffer_8
  assign xor_1_out = AI ^ DBI;  // XOR_Gate xor_1, 8 bits wide
  assign controlled_buffer_1_out = BXOr ? xor_1_out : 8'bz;  // Controlled_Buffer controlled_buffer_9
  Shifter shifter_1 (.in(AI), .\dist (DBI[2:0]), .out(shifter_1_out));
  Shifter #(.shift("lr")) shifter_2 (.in(AI), .\dist (DBI[2:0]), .out(shifter_2_out));
  assign not_1_out = ~AI;  // NOT_Gate not_1, 8 bits wide
  Adder adder_2 (.a(AI), .b({8{1'b0}}), .out(adder_2_out), .cin(1'b1));  // open: cout
  Subtractor subtractor_2 (.a(AI), .b({8{1'b0}}), .out(subtractor_2_out), .bin(1'b1));  // open: bout
  assign controlled_buffer_1_out = Shl ? shifter_1_out : 8'bz;  // Controlled_Buffer controlled_buffer_10
  assign controlled_buffer_1_out = Shr ? shifter_2_out : 8'bz;  // Controlled_Buffer controlled_buffer_11
  assign controlled_buffer_1_out = BNot ? not_1_out : 8'bz;  // Controlled_Buffer controlled_buffer_12
  assign controlled_buffer_1_out = Inc ? adder_2_out : 8'bz;  // Controlled_Buffer controlled_buffer_13
  assign controlled_buffer_1_out = Dec ? subtractor_2_out : 8'bz;  // Controlled_Buffer controlled_buffer_14
  Register register_1 (.D(controlled_buffer_1_out), .en(1'b1), .clk(Clk), .Q(register_1_q), .clr(Rst));
  assign DBO = OE ? register_1_q : 8'bz;  // Controlled_Buffer controlled_buffer_15
  nor nor_1 (Z, controlled_buffer_1_out[0], controlled_buffer_1_out[1], controlled_buffer_1_out[2], controlled_buffer_1_out[3], controlled_buffer_1_out[4], controlled_buffer_1_out[5], controlled_buffer_1_out[6], controlled_buffer_1_out[7]);
endmodule

module IR (
  input  [7:0] DI,
  input  WE,
  input  Clk,
  input  Reset,
  output [7:0] DO
);

  Register register_1 (.D(DI), .en(WE), .clk(Clk), .Q(DO), .clr(Reset));
endmodule

module AR (
  input  Clk,
  input  Rst,
  input  [7:0] ADLI,
  input  [7:0] ADHI,
  input  LWE,
  input  HWE,
  output [7:0] ADLO,
  output [7:0] ADHO
);

  Register register_1 (.D(ADLI), .en(LWE), .clk(Clk), .Q(ADLO), .clr(Rst));
  Register register_2 (.D(ADHI), .en(HWE), .clk(Clk), .Q(ADHO), .clr(Rst));
endmodule

module SP (
  input  [7:0] DI,
  input  OE,
  input  WE,
  input  Clk,
  input  Reset,
  output [7:0] DO
);

  wire [7:0] register_1_q;

  Register register_1 (.D(DI), .en(WE), .clk(Clk), .Q(register_1_q), .clr(Reset));
  assign DO = OE ? register_1_q : 8'bz;  // Controlled_Buffer controlled_buffer_1
endmodule

module JSD (
  input  WEI,
  input  JE,
  input  IJE,
  output WEO
);

  wire multiplexer_1_out, not_1_out;

  Multiplexer multiplexer_1 (.in0(JE), .in1(not_1_out), .out(multiplexer_1_out), .sel(IJE));
  Pull_Resistor #(.pull(1)) pull_resistor_1 (.node(multiplexer_1_out));
  not not_1 (not_1_out, JE);
  and and_1 (WEO, WEI, multiplexer_1_out);
endmodule

module SR (
  input  ZE,
  input  CE,
  input  EE,
  input  LE,
  input  GE,
  input  [7:0] DI,
  input  WE,
  input  Clk,
  input  Rst,
  output [7:0] DO,
  output FO,
  output IO,
  output HO
);

  Register register_1 (.D(DI), .en(WE), .clk(Clk), .Q(DO), .clr(Rst));
  assign FO = ZE ? DO[0] : 1'bz;  // Controlled_Buffer controlled_buffer_1
  assign FO = CE ? DO[1] : 1'bz;  // Controlled_Buffer controlled_buffer_2
  assign FO = EE ? DO[2] : 1'bz;  // Controlled_Buffer controlled_buffer_3
  assign FO = LE ? DO[3] : 1'bz;  // Controlled_Buffer controlled_buffer_4
  assign FO = GE ? DO[4] : 1'bz;  // Controlled_Buffer controlled_buffer_5

  assign HO = DO[7];
  assign IO = DO[6];
endmodule

module Const (
  input  OE1,
  output [7:0] D
);

  assign D = OE1 ? {8{1'b1}} : 8'bz;  // Controlled_Buffer controlled_buffer_1
endmodule
